// Logisim project 2307064.circ as structural Verilog: 3 circuits, main circuit main
module main (
);

  wire clock_1_out, cpu_1_r, cpu_1_w, Reset_out;
  wire [4:0] cpu_1_addr;
  wire [22:0] cpu_1_dataout, ram_1_data;

  Clock clock_1 (.out(clock_1_out));
  Button Reset (.out(Reset_out));
  CPU cpu_1 (
    .Clk(clock_1_out), .Reset(Reset_out), .R(cpu_1_r), .W(cpu_1_w), .Addr(cpu_1_addr), .DataIn(ram_1_data),
    .DataOut(cpu_1_dataout));  // open: BOOTHS_LOW, BOOTHS_High
  RAM #(.addrWidth(5), .dataWidth(23), .bus("separate")) ram_1 (
    .addr(cpu_1_addr), .din(cpu_1_dataout), .data(ram_1_data), .str(cpu_1_w), .clk(clock_1_out), .ld(cpu_1_r));  // open: sel, clr

  // Notes on the sheet:
  //   0 - AND
  //   1 - ADD
  //   2 - STO
  //   3 - OR
  //   4 - SUB
  //   5 - BUN
  //   6 - LDA
  //   7 - HLT
  //   8 - XOR
  //   9 - SHR
  //   A -ROR
  //   B - 2's Complement
  //   C - Upper Booths to AC
  //   D - BOOTHS_MULTIPLICATION
endmodule

module CPU (
  input  Clk,
  input  Reset,
  input  [22:0] DataIn,
  output [22:0] BOOTHS_LOW,
  output [22:0] BOOTHS_High,
  output R,
  output W,
  output [4:0] Addr,
  output [22:0] DataOut
);

  wire a0, a1, a2, and_1_out, and_2_out, b1, booth_s_multiplier_1_halt, bth, controlunit_1_c1,
       controlunit_1_c2, d1, d2, highBTH, LdA, LdA_from_MBR, LoadAc, LoadB, LoadMAR, lowBTH, not_1_out, STALL;
  wire [4:0] counter_1_q, multiplexer_1_out;
  wire [22:0] Ac, AcIn, ALU, ALUout, multiplexer_3_out, multiplexer_5_out;

  Multiplexer #(.width(5), .enable("false")) multiplexer_1 (
    .in0(counter_1_q), .in1(DataOut[4:0]), .out(multiplexer_1_out), .sel(d2));
  and and_1 (and_1_out, Clk, not_1_out);
  not not_1 (not_1_out, STALL);
  Counter #(.width(5), .max('h1f)) counter_1 (
    .load(controlunit_1_c2), .D(DataOut[4:0]), .count(controlunit_1_c1), .Q(counter_1_q), .clk(and_1_out),
    .clr(Reset));  // open: carry
  Register #(.width(5)) MAR (.D(multiplexer_1_out), .en(LoadMAR), .Q(Addr), .clk(and_1_out), .clr(Reset));
  Register #(.width(4)) IR (.D(DataOut[19:16]), .en(controlunit_1_c1), .clk(and_1_out), .clr(Reset));  // open: Q
  ControlUnit controlunit_1 (
    .IR(DataOut[19:16]), .Clk(and_1_out), .d1(d1), .c1(controlunit_1_c1), .R(R), .c2(controlunit_1_c2),
    .d2(d2), .b1(b1), .W(W), .LdAfrB(LdA_from_MBR), .Operation({a2, a1, a0}), .LoadAc(LdA), .Reset(Reset),
    .bth(bth), .lower_bths(lowBTH), .higher_bths(highBTH));
  Multiplexer #(.width(23), .enable("false")) multiplexer_2 (
    .in0(ALUout), .in1(DataOut), .out(AcIn), .sel(LdA_from_MBR));
  Multiplexer #(.width(23), .enable("false")) multiplexer_3 (.in0(DataIn), .in1(Ac), .out(multiplexer_3_out), .sel(b1));
  or or_1 (LoadMAR, d1, d2);
  Register #(.width(23)) MBR (.D(multiplexer_3_out), .en(LoadB), .Q(DataOut), .clk(and_1_out), .clr(Reset));
  Register #(.width(23)) u_Ac (.D(AcIn), .en(LoadAc), .Q(Ac), .clk(and_1_out), .clr(Reset));
  // _23_bit_ALU_main main_1: pin names not known; wires that end beside it: {a2, a1, a0}, Ac, DataOut, ALU
  or or_2 (LoadB, R, b1);
  or or_3 (LoadAc, LdA_from_MBR, LdA);
  Multiplexer #(.width(23), .enable("false")) multiplexer_4 (
    .in0(multiplexer_5_out), .in1(BOOTHS_High), .out(ALUout), .sel(highBTH));
  Booth_s_multiplier booth_s_multiplier_1 (
    .M_input(Ac), .Q_input(DataOut), .CLK(and_2_out), .halt(booth_s_multiplier_1_halt), .Lower(BOOTHS_LOW),
    .Higher(BOOTHS_High));  // open: Reset
  and and_2 (and_2_out, Clk, bth);
  Multiplexer #(.width(23), .enable("false")) multiplexer_5 (
    .in0(ALU), .in1(BOOTHS_LOW), .out(multiplexer_5_out), .sel(lowBTH));
  and and_3 (STALL, booth_s_multiplier_1_halt, bth);

  // Other names for the same wires on the sheet: clr = Reset; HIGH[22:0] = BOOTHS_High; LOW[22:0] = BOOTHS_LOW;
  //   MBRout[22:0] = DataOut; muxOUT[22:0] = ALUout
endmodule

// CU
module ControlUnit (
  input  [3:0] IR,
  input  Clk,
  input  Reset,
  output d1,
  output c1,
  output R,
  output c2,
  output d2,
  output [2:0] Operation,
  output b1,
  output W,
  output LoadAc,
  output LdAfrB,
  output lower_bths,
  output higher_bths,
  output bth
);

  wire and_1_out, decoder_1_out6, decoder_1_out7, decoder_1_out8, decoder_1_out9, decoder_1_out15,
       decoder_1_out16, decoder_1_out17, decoder_1_out18, decoder_1_out19, not_1_out, or_1_out;
  wire [5:0] counter_1_q;
  wire [7:0] rom_1_data;

  Counter #(.width(6), .max('h3f)) counter_1 (
    .load(rom_1_data[2]), .D({IR, 2'b11}), .count(rom_1_data[0]), .Q(counter_1_q), .clk(and_1_out),
    .clr(or_1_out));  // open: carry
  or or_1 (or_1_out, rom_1_data[1], Reset);
  and and_1 (and_1_out, Clk, not_1_out);
  ROM #(.addrWidth(6)) rom_1 (.addr(counter_1_q), .data(rom_1_data));  // open: sel
  not not_1 (not_1_out, decoder_1_out15);
  Decoder #(.select(5), .enable("false")) decoder_1 (
    .out1(d1), .out2(c1), .out3(R), .out4(c2), .out5(d2), .out6(decoder_1_out6), .out7(decoder_1_out7),
    .out8(decoder_1_out8), .out9(decoder_1_out9), .out10(b1), .out11(W), .out14(LdAfrB),
    .out15(decoder_1_out15), .out16(decoder_1_out16), .out17(decoder_1_out17), .out18(decoder_1_out18),
    .out19(decoder_1_out19), .out20(bth), .out21(lower_bths), .out22(higher_bths), .sel(rom_1_data[7:3]));  // open: out0, out12, out13, out23, out24, out25, out26, out27, out28, out29, out30, out31
  Priority_Encoder priority_encoder_1 (
    .in0(decoder_1_out6), .in1(decoder_1_out7), .in2(decoder_1_out8), .in3(decoder_1_out9),
    .in4(decoder_1_out16), .in5(decoder_1_out17), .in6(decoder_1_out18), .in7(decoder_1_out19),
    .out(Operation));  // open: en_in, gs, en_out
  or or_2 (LoadAc, decoder_1_out6, decoder_1_out7, decoder_1_out8, decoder_1_out9, lower_bths, decoder_1_out17, decoder_1_out18, decoder_1_out19, decoder_1_out16, higher_bths);

  // Notes on the sheet:
  //   contents of rom_1 (hex, n*v repeats v):
  //   9 19 14 29 19 31 2 29 19 39 2 29 51 59 2 29 19 41 2 29 19 49 2 21 2 2 2 29 19 71 2 78 29 79 29 29 19
  //   81 2 89 2 2 2 91 2 2 2 99 2 2 2 b1 2 2 2 29 19 a1 a1 a9 2
endmodule
